// Logisim project exercicio1.circ as structural Verilog: 5 circuits, main circuit main
module main (
  input  A0,
  input  A1,
  input  in_3,
  input  A2,
  input  A3,
  input  B0,
  input  B1,
  input  B2,
  input  B3
);

  wire decoder_2_a, decoder_2_b, decoder_2_c, decoder_2_d, decoder_2_e, decoder_2_f, decoder_2_g,
       decoder_3_a, decoder_3_b, decoder_3_c, decoder_3_d, decoder_3_e, decoder_3_f, decoder_3_g, decoder_a,
       decoder_b, decoder_c, decoder_d, decoder_e, decoder_f, decoder_g, somador_4b_s0, somador_4b_s1,
       somador_4b_s2, somador_4b_s3;

  codificador decoder (
    .E1(A3), .E2(A2), .E3(A1), .E4(A0), .a(decoder_a), .b(decoder_b), .c(decoder_c), .d(decoder_d),
    .e(decoder_e), .f(decoder_f), .g(decoder_g));
  somador_de_4_bits somador_4b (
    .A0(A0), .A1(A1), .A2(A2), .A3(A3), .B0(B0), .B1(B1), .B2(B2), .B3(B3), .C(in_3), .S0(somador_4b_s0),
    .S1(somador_4b_s1), .S2(somador_4b_s2), .S3(somador_4b_s3));  // open: Overflow
  codificador decoder_2 (
    .E1(B3), .E2(B2), .E3(B1), .E4(B0), .a(decoder_2_a), .b(decoder_2_b), .c(decoder_2_c), .d(decoder_2_d),
    .e(decoder_2_e), .f(decoder_2_f), .g(decoder_2_g));
  _7_Segment_Display u_7_segment_display_1 (
    .g(decoder_g), .f(decoder_f), .a(decoder_a), .b(decoder_b), .e(decoder_e), .d(decoder_d), .c(decoder_c));  // open: dp
  _7_Segment_Display u_7_segment_display_2 (
    .g(decoder_2_g), .f(decoder_2_f), .a(decoder_2_a), .b(decoder_2_b), .e(decoder_2_e), .d(decoder_2_d),
    .c(decoder_2_c));  // open: dp
  codificador decoder_3 (
    .E1(somador_4b_s3), .E2(somador_4b_s2), .E3(somador_4b_s1), .E4(somador_4b_s0), .a(decoder_3_a),
    .b(decoder_3_b), .c(decoder_3_c), .d(decoder_3_d), .e(decoder_3_e), .f(decoder_3_f), .g(decoder_3_g));
  _7_Segment_Display u_7_segment_display_3 (
    .g(decoder_3_g), .f(decoder_3_f), .a(decoder_3_a), .b(decoder_3_b), .e(decoder_3_e), .d(decoder_3_d),
    .c(decoder_3_c));  // open: dp

  // Notes on the sheet:
  //   Somador com exibição
endmodule

module codificador (
  input  E1,
  input  E2,
  input  E3,
  input  E4,
  output a,
  output b,
  output c,
  output d,
  output e,
  output f,
  output g
);

  wire and_1_out, and_2_out, and_3_out, and_4_out, and_5_out, and_6_out, and_7_out, and_8_out, and_9_out,
       and_10_out, and_11_out, and_12_out, and_13_out, and_14_out, and_15_out, and_16_out, and_17_out,
       and_18_out, and_19_out, and_20_out, and_21_out, and_22_out, and_23_out, and_24_out, and_25_out,
       and_26_out, and_27_out, and_28_out, and_29_out, and_30_out, and_31_out, and_32_out, and_33_out,
       and_34_out, not_1_out, not_2_out, not_3_out, not_4_out, not_5_out, not_6_out, not_7_out, not_8_out,
       not_9_out, not_10_out, not_11_out, not_12_out, not_13_out, not_14_out, not_15_out, not_16_out,
       not_17_out, not_18_out, not_19_out, not_20_out, not_21_out, not_22_out, not_23_out, not_24_out,
       not_25_out, not_26_out, not_27_out, not_28_out, not_29_out, not_30_out, not_31_out, not_32_out,
       not_33_out, not_34_out, not_35_out, not_36_out, not_37_out, not_38_out, not_39_out, not_40_out,
       not_41_out;

  not not_1 (not_1_out, E2);
  and and_1 (and_1_out, not_1_out, not_2_out);
  not not_2 (not_2_out, E4);
  not not_3 (not_3_out, E1);
  and and_2 (and_2_out, not_3_out, E3);
  not not_4 (not_4_out, E1);
  and and_3 (and_3_out, not_4_out, E2, E4);
  and and_4 (and_4_out, E2, E3);
  not not_5 (not_5_out, E2);
  and and_5 (and_5_out, E1, not_5_out, not_6_out);
  not not_6 (not_6_out, E3);
  and and_6 (and_6_out, E1, not_7_out);
  not not_7 (not_7_out, E4);
  not not_8 (not_8_out, E1);
  and and_7 (and_7_out, not_8_out, not_9_out);
  not not_9 (not_9_out, E2);
  not not_10 (not_10_out, E1);
  not not_11 (not_11_out, E3);
  and and_8 (and_8_out, not_10_out, not_11_out, not_12_out);
  not not_12 (not_12_out, E4);
  not not_13 (not_13_out, E2);
  and and_9 (and_9_out, not_13_out, not_14_out);
  not not_14 (not_14_out, E4);
  not not_15 (not_15_out, E1);
  and and_10 (and_10_out, not_15_out, E3, E4);
  and and_11 (and_11_out, E1, not_16_out, E4);
  not not_16 (not_16_out, E3);
  not not_17 (not_17_out, E1);
  and and_12 (and_12_out, not_17_out, not_18_out);
  not not_18 (not_18_out, E3);
  not not_19 (not_19_out, E1);
  and and_13 (and_13_out, not_19_out, E4);
  not not_20 (not_20_out, E3);
  and and_14 (and_14_out, not_20_out, E4);
  not not_21 (not_21_out, E1);
  and and_15 (and_15_out, not_21_out, E2);
  and and_16 (and_16_out, E1, not_22_out);
  not not_22 (not_22_out, E2);
  not not_23 (not_23_out, E1);
  and and_17 (and_17_out, not_23_out, not_24_out, not_25_out);
  not not_24 (not_24_out, E2);
  not not_25 (not_25_out, E4);
  not not_26 (not_26_out, E2);
  and and_18 (and_18_out, not_26_out, E3, E4);
  and and_19 (and_19_out, E2, not_27_out, E4);
  not not_27 (not_27_out, E3);
  and and_20 (and_20_out, E2, E3, not_28_out);
  not not_28 (not_28_out, E4);
  and and_21 (and_21_out, E1, not_29_out);
  not not_29 (not_29_out, E3);
  not not_30 (not_30_out, E2);
  and and_22 (and_22_out, not_30_out, not_31_out);
  not not_31 (not_31_out, E4);
  and and_23 (and_23_out, E3, not_32_out);
  not not_32 (not_32_out, E4);
  and and_24 (and_24_out, E1, E3);
  and and_25 (and_25_out, E1, E2);
  not not_33 (not_33_out, E3);
  and and_26 (and_26_out, not_33_out, not_34_out);
  not not_34 (not_34_out, E4);
  not not_35 (not_35_out, E1);
  and and_27 (and_27_out, not_35_out, E2);
  and and_28 (and_28_out, E1, not_36_out);
  not not_36 (not_36_out, E2);
  and and_29 (and_29_out, E1, E3);
  not not_37 (not_37_out, E2);
  and and_30 (and_30_out, not_37_out, E3);
  and and_31 (and_31_out, E3, not_38_out);
  not not_38 (not_38_out, E4);
  not not_39 (not_39_out, E1);
  and and_32 (and_32_out, not_39_out, E2, not_40_out);
  not not_40 (not_40_out, E3);
  and and_33 (and_33_out, E1, not_41_out);
  not not_41 (not_41_out, E2);
  and and_34 (and_34_out, E1, E4);
  or or_1 (b, and_7_out, and_8_out, and_9_out, and_10_out, and_11_out);
  or or_2 (c, and_12_out, and_13_out, and_14_out, and_15_out, and_16_out);
  or or_3 (d, and_17_out, and_18_out, and_19_out, and_20_out, and_21_out);
  or or_4 (e, and_22_out, and_23_out, and_24_out, and_25_out);
  or or_5 (f, and_26_out, and_27_out, and_28_out, and_29_out);
  or or_6 (g, and_30_out, and_31_out, and_32_out, and_33_out, and_34_out);
  or or_7 (a, and_1_out, and_2_out, and_3_out, and_4_out, and_5_out, and_6_out);

  // Notes on the sheet:
  //   Decodificador
endmodule

module meia_soma (
  input  A,
  input  B,
  output S,
  output Vai_um
);

  xor xor_1 (S, B, A);
  and and_1 (Vai_um, B, A);

  // Notes on the sheet:
  //   Meia soma
endmodule

module somador_completo (
  input  A,
  input  B,
  input  C,
  output S,
  output vai_um
);

  wire meia_soma_1_s, meia_soma_1_vai_um, meia_soma_2_vai_um;

  meia_soma meia_soma_1 (.A(A), .B(B), .S(meia_soma_1_s), .Vai_um(meia_soma_1_vai_um));
  meia_soma meia_soma_2 (.A(meia_soma_1_s), .B(C), .S(S), .Vai_um(meia_soma_2_vai_um));
  or or_1 (vai_um, meia_soma_2_vai_um, meia_soma_1_vai_um);

  // Notes on the sheet:
  //   Somador completo
endmodule

module somador_de_4_bits (
  input  C,
  input  A0,
  input  A1,
  input  A2,
  input  A3,
  input  B0,
  input  B1,
  input  B2,
  input  B3,
  output S0,
  output S1,
  output S2,
  output S3,
  output Overflow
);

  wire Somador_completo_2_vai_um, Somador_completo_3_vai_um, Somador_completo_vai_um;

  somador_completo Somador_completo (.A(A0), .B(B0), .C(C), .S(S0), .vai_um(Somador_completo_vai_um));
  somador_completo Somador_completo_2 (
    .A(A1), .B(B1), .C(Somador_completo_vai_um), .S(S1), .vai_um(Somador_completo_2_vai_um));
  somador_completo Somador_completo_3 (
    .A(A2), .B(B2), .C(Somador_completo_2_vai_um), .S(S2), .vai_um(Somador_completo_3_vai_um));
  somador_completo Somador_completo_4 (.A(A3), .B(B3), .C(Somador_completo_3_vai_um), .S(S3), .vai_um(Overflow));

  // Notes on the sheet:
  //   Últimos digitos $da matrícula: 83
  //   Somador de 4 bits
  //   30 ns
  //   50 ns
  //   20 ns
  //   40 ns
  //   60 ns
  //   70 ns
  //   80 ns
  //   90 ns
  //   Resultado:  8+3=11
endmodule
